# Fritzing sketch cp_IoT_circuit1 (saved by Fritzing 0.8.3b)
breadboards: 1

parts:
  R1 = Resistor [tolerance=±5% resistance=220 package=THT]
  S1 = Pushbutton [package="[THT]"]
  LED1 = LED - 5mm [color="Red (633nm)" package="5 mm [THT]"]
  J1 = male pin header, 4 pins [form="♂ (male)"]
  LED2 = LED - 5mm [color="Red (633nm)" package="5 mm [THT]"]
  Raspberry_Pi_rev1 = Raspberry Pi rev1

nets:
  N1: R1.Pin_0, S1.Pin_1, S1.Pin_2
  N2: R1.Pin_1, LED1.anode, J1.pin1, Raspberry_Pi_rev1.GPIO_23
  N3: S1.Pin_3, S1.Pin_4, J1.pin3, Raspberry_Pi_rev1.3V3
  N4: LED1.cathode, J1.pin4, LED2.cathode, Raspberry_Pi_rev1.GND
  N5: J1.pin2, LED2.anode, Raspberry_Pi_rev1.GPIO_17
