# Fritzing sketch plant_watering_Arduino_cct (saved by Fritzing 0.8.3b)
circuit board: 5.09023cm x 5.72654cm
breadboards: 2

parts:
  U1 = HIH-4030 [package=hih-4030]
  VCC1 = Battery
  M1 = DC Motor
  IC1 = L293D [package=THT]
  Raspberry_Pi_rev1 = Raspberry Pi rev2

nets:
  GND: U1.GND, VCC1.-, IC1.0V, Raspberry_Pi_rev1.GND
  N1: U1.OUT, Raspberry_Pi_rev1.GPIO_18
  N2: U1.VCC, VCC1.+, IC1.+Vmotor, IC1.+V
  N3: M1.pin_1, IC1.Out_2_(_Controlled_by_Enable_1_)
  N4: M1.pin_2, IC1.Out_1_(_Controlled_by_Enable_1_)
  N5: IC1.Enable_1, Raspberry_Pi_rev1.GIPO_2
  N6: IC1.In_1, Raspberry_Pi_rev1.GPIO_23
  N7: IC1.In_2, Raspberry_Pi_rev1.GIPO_3
