# Fritzing sketch plant_watering_arduino_cct (saved by Fritzing 0.8.3b)
circuit board: 5.09023cm x 5.72654cm
breadboards: 3

parts:
  U1 = HIH-4030 [package=hih-4030]
  Nano1 = Arduino Nano v2.3
  VCC1 = Battery
  Bluetooth_Module = Bluetooth Mate Silver
  M1 = DC Motor
  IC1 = L293D [package=THT]

nets:
  GND: U1.GND, Nano1.GND, VCC1.-, Bluetooth_Module.GND, IC1.0V
  N1: U1.OUT, Nano1.D2
  VCC: U1.VCC, Nano1.VIN, VCC1.+, Bluetooth_Module.VCC, IC1.+Vmotor, IC1.+V
  N2: Nano1.D1TX, Bluetooth_Module.RX_5V
  N3: Nano1.D0RX, Bluetooth_Module.TX_5V
  N4: Nano1.D3, IC1.In_1
  N5: Nano1.D4, IC1.In_2
  N6: Nano1.D5, IC1.Enable_1
  N7: M1.pin_1, IC1.Out_2_(_Controlled_by_Enable_1_)
  N8: M1.pin_2, IC1.Out_1_(_Controlled_by_Enable_1_)
